// Digital circuit main_cpu.dig as structural Verilog
module main_cpu (
  input  [7:0] M,
  input  [7:0] N,
  input  [13:0] progIn,
  input  reset,
  input  progLoad,
  input  start,
  input  result,
  input  clk,
  output valid,
  output done,
  output [7:0] \output ,
  output [13:0] out_12,
  output [7:0] out_13,
  output [7:0] out_14,
  output [7:0] out_15,
  output [7:0] out_16,
  output [7:0] out_17,
  output [7:0] out_18,
  output [7:0] out_19,
  output [7:0] out_20,
  output [7:0] out_21,
  output [7:0] out_22,
  output [7:0] out_23,
  output [7:0] out_24,
  output [2:0] out_25,
  output [1:0] out_26,
  output [1:0] out_27,
  output [1:0] out_28,
  output [1:0] out_29,
  output [1:0] out_30,
  output [2:0] out_31,
  output out_32,
  output [7:0] out_33,
  output [7:0] out_34,
  output [7:0] out_35,
  output [7:0] out_36,
  output [4:0] out_37,
  output [7:0] out_38,
  output [7:0] out_39,
  output [7:0] out_40,
  output [7:0] out_41,
  output [7:0] out_42,
  output [7:0] out_43,
  output [15:0] out_44,
  output [7:0] out_45,
  output [15:0] out_46,
  output [7:0] out_47,
  output [5:0] out_48
);

  wire and_1_out, and_2_out, and_3_out, and_4_out, and_5_out, clear, comp_eq, comp_gt, comp_lt,
       comparator_2_eq, comparator_2_lt, comparator_3_gt, comparator_4_eq, eq, f0, f1, f2, f3, fact_0_state,
       fact_1_state, fact_load_rRAM, gt, index_gt_accB, LCM__gt, LCM__lt, LCM_finish, load__eq, load__gt,
       load__lt, load_A, load_B, load_C, load_D, load_instruction, load_LCMa, load_LCMb, load_PC, load_rRAM,
       lt, m0, m1, m2, m3, max_0_state, max_1_state, multiplexer_1_out, multiplexer_2_out, multiplexer_7_out,
       multiplexer_8_out, multiplexer_9_out, multiplexer_10_out, multiplexer_11_out, multiplexer_12_out,
       multiplexer_13_out, multiplexer_24_out, multiplexer_27_out, multiplexer_33_out, multiplexer_38_out,
       n_lt__eq_2, not_1_out, not_2_out, not_3_out, not_4_out, not_5_out, not_6_out, not_7_out, not_8_out,
       not_9_out, not_10_out, not_12_out, not_13_out, op0, op1, op2, op3, op4, op5, op6, op7, op8, op9, op10,
       op11, op12, op13, op14, op16, op17, op18, op19, op20, op21, op22, op23, op24, op25, op26, op27, op28,
       op29, op30, op31, op32, op33, op34, op35, op36, op37, op38, op39, op40, op41, op42, op43, op44, op45,
       op46, op47, op48, op49, op50, op51, op52, op53, op54, op55, op56, op57, op58, op59, op60, op61, op62,
       op63, or_9_out, or_13_out, or_14_out, or_17_out, or_18_out, or_19_out, or_20_out, or_22_out,
       prime_list_d, Q0, Q1, Q2, Q3, Q4, reminder_eq, rRAM_overflow, sel_PC, T0, T2, T3, T4, T6, T7, T8, T9,
       T10, T11, T12, T13, T14, T15, T16, T17, T18, T19, T20, T21, T22, T23, T24, T25, T26, T27, T28, T29,
       T30;
  wire [4:0] decode;
  wire [7:0] A, A_B, A_B_t_t_t, A_B_t_t_t_t, A_gt__gt__gt_B, A_gt__gt_B, A_lt__lt__lt_B, A_lt__lt_B, AandB,
       add_1_s, add_2_s, AorB, AxorB, div_1_r, fact_output, multiplexer_3_out, multiplexer_4_out,
       multiplexer_5_out, multiplexer_6_out, multiplexer_15_out, multiplexer_16_out, multiplexer_17_out,
       multiplexer_18_out, multiplexer_19_out, multiplexer_20_out, multiplexer_21_out, multiplexer_22_out,
       multiplexer_23_out, multiplexer_25_out, multiplexer_29_out, multiplexer_30_out, multiplexer_31_out,
       multiplexer_31_out_2, multiplexer_34_out, multiplexer_35_out, multiplexer_36_out, multiplexer_37_out,
       n_1, pRAM_max_index_address, sub_2_s, sub_3_s;
  wire [13:8] pRAM_d1;
  wire [15:0] mul_1_mul, multiplexer_28_out;
  wire [31:16] mul_1_mul_2;

  Decoder #(.Selector_Bits(5)) decoder_1 (
    .sel(out_37), .out_0(T0), .out_1(load_instruction), .out_2(T2), .out_3(T3), .out_4(T4), .out_5(load_C),
    .out_6(T6), .out_7(T7), .out_8(T8), .out_9(T9), .out_10(T10), .out_11(T11), .out_12(T12), .out_13(T13),
    .out_14(T14), .out_15(T15), .out_16(T16), .out_17(T17), .out_18(T18), .out_19(T19), .out_20(T20),
    .out_21(T21), .out_22(T22), .out_23(T23), .out_24(T24), .out_25(T25), .out_26(T26), .out_27(T27),
    .out_28(T28), .out_29(T29), .out_30(T30), .out_31(done));
  Decoder #(.Selector_Bits(6)) decoder_2 (
    .sel(out_48), .out_0(op0), .out_1(op1), .out_2(op2), .out_3(op3), .out_4(op4), .out_5(op5), .out_6(op6),
    .out_7(op7), .out_8(op8), .out_9(op9), .out_10(op10), .out_11(op11), .out_12(op12), .out_13(op13),
    .out_14(op14), .out_15(out_32), .out_16(op16), .out_17(op17), .out_18(op18), .out_19(op19),
    .out_20(op20), .out_21(op21), .out_22(op22), .out_23(op23), .out_24(op24), .out_25(op25), .out_26(op26),
    .out_27(op27), .out_28(op28), .out_29(op29), .out_30(op30), .out_31(op31), .out_32(op32), .out_33(op33),
    .out_34(op34), .out_35(op35), .out_36(op36), .out_37(op37), .out_38(op38), .out_39(op39), .out_40(op40),
    .out_41(op41), .out_42(op42), .out_43(op43), .out_44(op44), .out_45(op45), .out_46(op46), .out_47(op47),
    .out_48(op48), .out_49(op49), .out_50(op50), .out_51(op51), .out_52(op52), .out_53(op53), .out_54(op54),
    .out_55(op55), .out_56(op56), .out_57(op57), .out_58(op58), .out_59(op59), .out_60(op60), .out_61(op61),
    .out_62(op62), .out_63(op63));
  Multiplexer #(.Selector_Bits(5)) multiplexer_1 (
    .sel(out_37), .in_0(1'b0), .in_1(1'b0), .in_2(decode[4]), .in_3(1'b0), .in_4(1'b0), .in_5(1'b0),
    .in_6(1'b0), .in_7(1'b0), .in_8(1'b0), .in_9(1'b1), .in_10(1'b1), .in_11(1'b0), .in_12(1'b1),
    .in_13(1'b0), .in_14(1'b0), .in_15(1'b0), .in_16(1'b0), .in_17(1'b0), .in_18(1'b0), .in_19(1'b1),
    .in_20(1'b1), .in_21(1'b1), .in_22(1'b0), .in_23(1'b0), .in_24(not_1_out), .in_25(not_2_out),
    .in_26(not_3_out), .in_27(1'b0), .in_28(1'b0), .in_29(1'b1), .in_30(1'b1), .in_31(1'b1),
    .out(multiplexer_1_out));
  not not_1 (not_1_out, rRAM_overflow);
  not not_2 (not_2_out, f3);
  not not_3 (not_3_out, m3);
  D_FF u_Q4 (.D(multiplexer_1_out), .C(clk), .Q(Q4));  // open: nQ
  Div #(.remainderPositive("false"), .Bits(8)) div_1 (.a(out_14), .b(out_15), .r(div_1_r));  // open: q
  not not_4 (not_4_out, rRAM_overflow);
  not not_5 (not_5_out, f3);
  not not_6 (not_6_out, m3);
  Comparator #(.Signed("true"), .Bits(8)) comp (.a(out_14), .b(out_15), .gt(comp_gt), .eq(comp_eq), .lt(comp_lt));
  ROM #(.AddrBits(8)) prime_list (.A(out_14), .sel(1'b1), .D(prime_list_d));
  Comparator #(.Bits(8)) reminder (.a(div_1_r), .b({8{1'b0}}), .eq(reminder_eq));  // open: gt, lt
  Multiplexer #(.Selector_Bits(5)) multiplexer_2 (
    .sel(out_37), .in_0(1'b0), .in_1(1'b0), .in_2(decode[3]), .in_3(op14), .in_4(1'b0), .in_5(op13),
    .in_6(1'b0), .in_7(1'b0), .in_8(1'b1), .in_9(1'b0), .in_10(1'b0), .in_11(1'b1), .in_12(1'b0),
    .in_13(1'b0), .in_14(1'b0), .in_15(1'b0), .in_16(1'b0), .in_17(1'b0), .in_18(1'b0), .in_19(1'b0),
    .in_20(1'b0), .in_21(1'b0), .in_22(1'b0), .in_23(1'b0), .in_24(not_4_out), .in_25(not_5_out),
    .in_26(not_6_out), .in_27(1'b0), .in_28(1'b0), .in_29(1'b1), .in_30(1'b1), .in_31(1'b1),
    .out(multiplexer_2_out));
  Multiplexer #(.Selector_Bits(3), .Bits(8)) multiplexer_3 (
    .sel(out_25), .in_0(out_47), .in_1(out_15), .in_2(out_16), .in_3(out_17), .in_4(out_35), .in_5(out_18),
    .in_6(out_20), .in_7({8{1'b0}}), .out(multiplexer_3_out));
  Multiplexer #(.Selector_Bits(2), .Bits(8)) multiplexer_4 (
    .sel(out_26), .in_0(out_47), .in_1(out_14), .in_2(out_17), .in_3({8{1'b0}}), .out(multiplexer_4_out));
  Multiplexer #(.Selector_Bits(2), .Bits(8)) multiplexer_5 (
    .sel(out_27), .in_0(out_14), .in_1(M), .in_2(N), .in_3({8{1'b0}}), .out(multiplexer_5_out));
  Multiplexer #(.Selector_Bits(2), .Bits(8)) multiplexer_6 (
    .sel(out_28), .in_0(out_14), .in_1(M), .in_2(N), .in_3({8{1'b0}}), .out(multiplexer_6_out));
  D_FF u_Q3 (.D(multiplexer_2_out), .C(clk), .Q(Q3));  // open: nQ
  Register #(.Bits(8)) accA (.D(multiplexer_3_out), .C(clk), .en(load_A), .Q(out_14));
  Register #(.Bits(8)) accB (.D(multiplexer_4_out), .C(clk), .en(load_B), .Q(out_15));
  Register #(.Bits(8)) regC (.D(multiplexer_5_out), .C(clk), .en(load_C), .Q(out_16));
  Register #(.Bits(8)) regD (.D(multiplexer_6_out), .C(clk), .en(load_D), .Q(out_17));
  Multiplexer #(.Selector_Bits(2)) multiplexer_7 (
    .sel(out_29), .in_0(comp_eq), .in_1(prime_list_d), .in_2(reminder_eq), .in_3(1'b0),
    .out(multiplexer_7_out));
  Multiplexer #(.Selector_Bits(5)) multiplexer_8 (
    .sel(out_37), .in_0(1'b0), .in_1(1'b0), .in_2(decode[2]), .in_3(op14), .in_4(1'b0), .in_5(op13),
    .in_6(1'b0), .in_7(1'b0), .in_8(1'b1), .in_9(1'b0), .in_10(1'b0), .in_11(1'b1), .in_12(1'b0),
    .in_13(1'b0), .in_14(1'b0), .in_15(1'b0), .in_16(1'b0), .in_17(1'b0), .in_18(1'b0), .in_19(1'b1),
    .in_20(1'b1), .in_21(1'b1), .in_22(1'b0), .in_23(1'b0), .in_24(1'b0), .in_25(1'b0), .in_26(1'b0),
    .in_27(1'b0), .in_28(1'b0), .in_29(1'b1), .in_30(1'b1), .in_31(1'b1), .out(multiplexer_8_out));
  Multiplexer multiplexer_9 (.sel(T24), .in_0(comp_gt), .in_1(1'b0), .out(multiplexer_9_out));
  Multiplexer multiplexer_10 (.sel(T24), .in_0(multiplexer_7_out), .in_1(1'b0), .out(multiplexer_10_out));
  Multiplexer multiplexer_11 (.sel(T24), .in_0(comp_lt), .in_1(1'b0), .out(multiplexer_11_out));
  D_FF u_Q2 (.D(multiplexer_8_out), .C(clk), .Q(Q2));  // open: nQ
  Multiplexer #(.Selector_Bits(5)) multiplexer_12 (
    .sel(out_37), .in_0(1'b0), .in_1(1'b1), .in_2(decode[1]), .in_3(1'b0), .in_4(1'b0), .in_5(op13),
    .in_6(1'b0), .in_7(1'b0), .in_8(1'b1), .in_9(1'b0), .in_10(1'b0), .in_11(1'b0), .in_12(1'b1),
    .in_13(1'b0), .in_14(1'b0), .in_15(1'b0), .in_16(1'b0), .in_17(1'b0), .in_18(1'b0), .in_19(1'b0),
    .in_20(1'b0), .in_21(1'b1), .in_22(1'b0), .in_23(1'b0), .in_24(1'b0), .in_25(1'b0), .in_26(not_7_out),
    .in_27(1'b0), .in_28(1'b0), .in_29(result), .in_30(1'b1), .in_31(1'b1), .out(multiplexer_12_out));
  not not_7 (not_7_out, m3);
  Register u_gt (.D(multiplexer_9_out), .C(clk), .en(load__gt), .Q(gt));
  Register u_eq (.D(multiplexer_10_out), .C(clk), .en(load__eq), .Q(eq));
  Register u_lt (.D(multiplexer_11_out), .C(clk), .en(load__lt), .Q(lt));
  D_FF u_Q1 (.D(multiplexer_12_out), .C(clk), .Q(Q1));  // open: nQ
  or or_1 (load_PC, T2, T24);
  or or_2 (load_A, T3, T15);
  or or_3 (load_B, T4, T13);
  or or_4 (load_D, T6, T14);
  or or_5 (load_rRAM, T7, T21, fact_load_rRAM, T22, T24, T26);
  or or_6 (load__eq, T16, T17, T18, T24);
  or or_7 (load__gt, T16, T24);
  or or_8 (load__lt, T16, T24);
  not not_8 (not_8_out, op13);
  not not_9 (not_9_out, result);
  not not_10 (not_10_out, result);
  Multiplexer #(.Selector_Bits(5)) multiplexer_13 (
    .sel(out_37), .in_0(start), .in_1(1'b0), .in_2(decode[0]), .in_3(1'b1), .in_4(1'b1), .in_5(not_8_out),
    .in_6(1'b1), .in_7(1'b1), .in_8(1'b1), .in_9(1'b0), .in_10(1'b1), .in_11(1'b0), .in_12(1'b1),
    .in_13(1'b1), .in_14(1'b1), .in_15(1'b1), .in_16(1'b1), .in_17(1'b1), .in_18(1'b1), .in_19(1'b0),
    .in_20(LCM_finish), .in_21(1'b0), .in_22(1'b1), .in_23(1'b1), .in_24(1'b0), .in_25(1'b1), .in_26(m3),
    .in_27(1'b0), .in_28(1'b0), .in_29(not_9_out), .in_30(rRAM_overflow), .in_31(not_10_out),
    .out(multiplexer_13_out));
  Multiplexer #(.Bits(5)) multiplexer_14 (.sel(reset), .in_0({Q4, Q3, Q2, Q1, Q0}), .in_1(5'b11000), .out(out_37));
  D_FF u_Q0 (.D(multiplexer_13_out), .C(clk), .Q(Q0));  // open: nQ
  Multiplexer #(.Bits(8)) multiplexer_15 (.sel(f3), .in_0(8'hb), .in_1(8'ha), .out(multiplexer_15_out));
  Multiplexer #(.Selector_Bits(2), .Bits(8)) multiplexer_16 (
    .sel(out_30), .in_0(out_14), .in_1(out_42), .in_2(out_43), .in_3({8{1'b0}}), .out(multiplexer_16_out));
  Multiplexer #(.Bits(8)) multiplexer_17 (.sel(T26), .in_0(multiplexer_15_out), .in_1(8'h9), .out(multiplexer_17_out));
  ROM #(.AddrBits(6), .Bits(3)) rom_1 (.A(out_48), .sel(1'b1), .D(out_25));
  ROM #(.AddrBits(6), .Bits(2)) rom_2 (.A(out_48), .sel(1'b1), .D(out_26));
  ROM #(.AddrBits(6), .Bits(2)) rom_3 (.A(out_48), .sel(1'b1), .D(out_27));
  ROM #(.AddrBits(6), .Bits(2)) rom_4 (.A(out_48), .sel(1'b1), .D(out_28));
  ROM #(.AddrBits(6), .Bits(2)) rom_5 (.A(out_48), .sel(1'b1), .D(out_29));
  ROM #(.AddrBits(5), .Bits(2)) rom_6 (.A(out_37), .sel(1'b1), .D(out_30));
  ROM #(.AddrBits(5), .Bits(3)) rom_7 (.A(out_37), .sel(1'b1), .D(out_31));
  Multiplexer #(.Bits(8)) multiplexer_18 (
    .sel(T25), .in_0(multiplexer_16_out), .in_1(fact_output), .out(multiplexer_18_out));
  Multiplexer #(.Selector_Bits(3), .Bits(8)) multiplexer_19 (
    .sel(out_31), .in_0(out_47), .in_1(8'he), .in_2(8'hf), .in_3({4'b0000, out_19[3:0]}),
    .in_4({4'b0000, out_47[3:0]}), .in_5({4'b0000, out_47[7:4]}), .in_6(multiplexer_17_out),
    .in_7({8{1'b0}}), .out(multiplexer_19_out));
  Multiplexer #(.Bits(8)) multiplexer_20 (
    .sel(T26), .in_0(multiplexer_18_out), .in_1(out_34), .out(multiplexer_20_out));
  not not_11 (clear, start);
  Multiplexer #(.Bits(8)) multiplexer_21 (.sel(out_32), .in_0(out_13), .in_1(out_47), .out(multiplexer_21_out));
  or or_9 (or_9_out, T30, T12, T19);
  or or_10 (valid, T29, T30, done);
  or or_11 (load_LCMa, T12, T20);
  or or_12 (load_LCMb, T19, T20);
  RAMDualAccess #(.AddrBits(8), .Bits(8)) rRAM (
    .str(load_rRAM), .C(clk), .ld(or_9_out), .A1(multiplexer_19_out), .Din1(multiplexer_20_out), .A2(out_47),
    .D1(\output ), .D2(out_18));
  Multiplexer #(.Bits(8)) multiplexer_22 (
    .sel(T26), .in_0(multiplexer_21_out), .in_1(pRAM_max_index_address), .out(multiplexer_22_out));
  Counter #(.Bits(8)) counter_1 (.en(progLoad), .C(clk), .clr(reset), .out(out_13));  // open: ovf
  RAMDualAccess #(.AddrBits(8), .Bits(14)) pRAM (
    .str(progLoad), .C(clk), .ld(1'b1), .A1(multiplexer_22_out), .Din1(progIn), .A2(out_24),
    .D1({pRAM_d1, out_35}), .D2(out_12));
  Add #(.Bits(8)) add_1 (.a(out_33), .b(8'h1), .c_i(1'b0), .s(add_1_s));  // open: c_o
  not not_12 (not_12_out, index_gt_accB);
  Sub #(.Bits(8)) sub_1 (.a(out_45), .b(8'h1), .c_i(1'b0), .s(n_1));  // open: c_o
  Multiplexer #(.Bits(8)) multiplexer_23 (.sel(m0), .in_0(add_1_s), .in_1(out_14), .out(multiplexer_23_out));
  or or_13 (or_13_out, m0, m1);
  Multiplexer #(.Selector_Bits(2)) multiplexer_24 (
    .sel({max_1_state, max_0_state}), .in_0(1'b0), .in_1(not_12_out), .in_2(1'b1), .in_3(1'b0),
    .out(multiplexer_24_out));
  Comparator #(.Bits(8)) comparator_1 (.a(out_33), .b(out_15), .lt(index_gt_accB));  // open: gt, eq
  D_FF d_ff_1 (.D(multiplexer_24_out), .C(clk), .Q(max_1_state));  // open: nQ
  Multiplexer #(.Bits(8)) multiplexer_25 (
    .sel(f1), .in_0({{5{1'b0}}, out_14[2:0]}), .in_1(n_1), .out(multiplexer_25_out));
  or or_14 (or_14_out, f0, f1);
  Comparator #(.Bits(8)) comparator_2 (.a(out_45), .b(8'h2), .eq(comparator_2_eq), .lt(comparator_2_lt));  // open: gt
  Seven_Seg_Hex seven_seg_hex_1 (.d(\output [7:4]), .dp(1'b0));
  ROM #(.AddrBits(6), .Bits(5)) nextstate_decode (.A(out_48), .sel(1'b1), .D(decode));
  Register #(.Bits(8)) index (.D(multiplexer_23_out), .C(clk), .en(or_13_out), .Q(out_33));
  Register #(.Bits(8)) u_n (.D(multiplexer_25_out), .C(clk), .en(or_14_out), .Q(out_45));
  or or_15 (n_lt__eq_2, comparator_2_eq, comparator_2_lt);
  or or_16 (fact_load_rRAM, f2, f3);
  Seven_Seg_Hex seven_seg_hex_2 (.d(\output [3:0]), .dp(1'b0));
  Multiplexer #(.Bits(8)) multiplexer_26 (.sel(m0), .in_0(out_33), .in_1(out_14), .out(pRAM_max_index_address));
  Multiplexer #(.Selector_Bits(2)) multiplexer_27 (
    .sel({max_1_state, max_0_state}), .in_0(T26), .in_1(index_gt_accB), .in_2(1'b1), .in_3(1'b0),
    .out(multiplexer_27_out));
  Mul #(.Bits(16)) mul_1 (.a(out_46), .b({{8{1'b0}}, n_1}), .mul({mul_1_mul_2, mul_1_mul}));
  Comparator #(.Signed("true"), .Bits(8)) comparator_3 (.a(out_35), .b(out_34), .gt(comparator_3_gt));  // open: eq, lt
  D_FF d_ff_2 (.D(multiplexer_27_out), .C(clk), .Q(max_0_state));  // open: nQ
  Multiplexer #(.Bits(16)) multiplexer_28 (
    .sel(f0), .in_0(mul_1_mul), .in_1({{13{1'b0}}, out_14[2:0]}), .out(multiplexer_28_out));
  or or_17 (or_17_out, f0, f1);
  and and_1 (and_1_out, op19, eq);
  and and_2 (and_2_out, op20, gt);
  and and_3 (and_3_out, op21, lt);
  or or_18 (or_18_out, eq, gt);
  or or_19 (or_19_out, eq, lt);
  Register #(.Bits(8)) max (.D(out_35), .C(clk), .en(comparator_3_gt), .Q(out_34));
  Decoder #(.Selector_Bits(2)) decoder_3 (
    .sel({max_1_state, max_0_state}), .out_0(m0), .out_1(m1), .out_2(m2), .out_3(m3));
  Register #(.Bits(16)) fact (.D(multiplexer_28_out), .C(clk), .en(or_17_out), .Q(out_46));
  Multiplexer #(.Bits(8)) multiplexer_29 (.sel(T24), .in_0(add_2_s), .in_1({8{1'b0}}), .out(multiplexer_29_out));
  Decoder #(.Selector_Bits(2)) decoder_4 (
    .sel({fact_1_state, fact_0_state}), .out_0(f0), .out_1(f1), .out_2(f2), .out_3(f3));
  and and_4 (and_4_out, op22, or_18_out);
  and and_5 (and_5_out, op23, or_19_out);
  Comparator #(.Signed("true"), .Bits(16)) comparator_4 (
    .a(out_46), .b({16{1'b0}}), .eq(comparator_4_eq));  // open: gt, lt
  Multiplexer #(.Bits(8)) multiplexer_30 (
    .sel(sel_PC), .in_0(multiplexer_29_out), .in_1(out_47), .out(multiplexer_30_out));
  Multiplexer #(.Bits(16)) multiplexer_31 (
    .sel(comparator_4_eq), .in_0(out_46), .in_1(16'h1), .out({multiplexer_31_out_2, multiplexer_31_out}));
  Sub #(.Bits(8)) sub_2 (.a(out_38), .b(out_39), .c_i(1'b0), .s(sub_2_s));  // open: c_o
  Sub #(.Bits(8)) sub_3 (.a(out_39), .b(out_38), .c_i(1'b0), .s(sub_3_s));  // open: c_o
  Mul #(.Bits(8)) mul_2 (.a(out_40), .b(out_41), .mul(out_44));
  Register #(.Bits(8)) u_A (.D(\output ), .C(clk), .en(T12), .Q(out_40));
  Register #(.Bits(8)) B (.D(\output ), .C(clk), .en(T19), .Q(out_41));
  Multiplexer #(.Bits(8)) multiplexer_32 (
    .sel(f3), .in_0(multiplexer_31_out), .in_1(multiplexer_31_out_2), .out(fact_output));
  Multiplexer #(.Selector_Bits(2)) multiplexer_33 (
    .sel({fact_1_state, fact_0_state}), .in_0(1'b0), .in_1(n_lt__eq_2), .in_2(1'b1), .in_3(1'b0),
    .out(multiplexer_33_out));
  Register #(.Bits(8)) register_1 (.D(multiplexer_30_out), .C(clk), .en(load_PC), .Q(out_24));
  or or_20 (or_20_out, op18, and_1_out, and_2_out, and_3_out, and_4_out, and_5_out);
  Multiplexer #(.Bits(8)) multiplexer_34 (.sel(LCM__gt), .in_0(out_38), .in_1(sub_2_s), .out(multiplexer_34_out));
  Multiplexer #(.Bits(8)) multiplexer_35 (.sel(LCM__lt), .in_0(out_39), .in_1(sub_3_s), .out(multiplexer_35_out));
  Div #(.Bits(16)) div_2 (.a(out_44), .b({{8{1'b0}}, out_38}), .q({out_43, out_42}));  // open: r
  D_FF d_ff_3 (.D(multiplexer_33_out), .C(clk), .Q(fact_1_state));  // open: nQ
  Add #(.Bits(8)) add_2 (.a(out_24), .b(8'h1), .c_i(1'b0), .s(add_2_s));  // open: c_o
  Multiplexer #(.Bits(8)) multiplexer_36 (
    .sel(T12), .in_0(multiplexer_34_out), .in_1(\output ), .out(multiplexer_36_out));
  Multiplexer #(.Bits(8)) multiplexer_37 (
    .sel(T19), .in_0(multiplexer_35_out), .in_1(\output ), .out(multiplexer_37_out));
  Multiplexer #(.Selector_Bits(2)) multiplexer_38 (
    .sel({fact_1_state, fact_0_state}), .in_0(T25), .in_1(not_13_out), .in_2(1'b1), .in_3(1'b0),
    .out(multiplexer_38_out));
  not not_13 (not_13_out, n_lt__eq_2);
  and and_6 (sel_PC, or_20_out, T2);
  Register #(.Bits(8)) LCMa (.D(multiplexer_36_out), .C(clk), .en(load_LCMa), .Q(out_38));
  Register #(.Bits(8)) LCMb (.D(multiplexer_37_out), .C(clk), .en(load_LCMb), .Q(out_39));
  Comparator #(.Bits(8)) comparator_5 (.a(out_38), .b(out_39), .gt(LCM__gt), .eq(LCM_finish), .lt(LCM__lt));
  D_FF d_ff_4 (.D(multiplexer_38_out), .C(clk), .Q(fact_0_state));  // open: nQ
  Add #(.Bits(8)) add_3 (.a(out_14), .b(out_15), .c_i(1'b0), .s(out_21));  // open: c_o
  Sub #(.Bits(8)) sub_4 (.a(out_14), .b(out_15), .c_i(1'b0), .s(out_22));  // open: c_o
  assign AandB = out_14 & out_15;  // And and_7, 8 bits wide
  assign AorB = out_14 | out_15;  // Or or_21, 8 bits wide
  assign AxorB = out_14 ^ out_15;  // XOr xor_1, 8 bits wide
  BarrelShifter #(.Bits(8)) barrelshifter_1 (.in(out_14), .shift(out_15[3:0]), .out(A_lt__lt_B));
  BarrelShifter #(.Bits(8), .direction("right")) barrelshifter_2 (.in(out_14), .shift(out_15[3:0]), .out(A_gt__gt_B));
  ROM #(.AddrBits(6), .Bits(8)) rom_8 (.A({out_14[2:0], out_15[2:0]}), .sel(1'b1), .D(A_B_t_t_t_t));
  Register #(.Bits(14)) register_2 (.D(out_12), .C(clk), .en(load_instruction), .Q({out_48, out_47}));
  Multiplexer #(.Selector_Bits(4), .Bits(8)) multiplexer_39 (
    .sel(out_48[3:0]), .in_0(out_21), .in_1(out_22), .in_2(out_23), .in_3(A_B_t_t_t), .in_4(A_B),
    .in_5(A_B_t_t_t_t), .in_6({8{1'b0}}), .in_7({8{1'b0}}), .in_8(A), .in_9(AandB), .in_10(AorB),
    .in_11(AxorB), .in_12(A_lt__lt_B), .in_13(A_lt__lt__lt_B), .in_14(A_gt__gt_B), .in_15(A_gt__gt__gt_B),
    .out(out_20));
  or or_22 (or_22_out, T30, T24);
  Counter #(.Bits(4)) counter_2 (.en(or_22_out), .C(clk), .clr(reset), .out(out_19[3:0]), .ovf(rRAM_overflow));
  Mul #(.Bits(4)) mul_3 (.a(out_14[3:0]), .b(out_15[3:0]), .mul(out_23));
  Div #(.Bits(8)) div_3 (.a(out_14), .b(out_15), .q(A_B_t_t_t), .r(A_B));
  not not_14 (A[0], out_14[0]);
  not not_15 (A[1], out_14[1]);
  not not_16 (A[2], out_14[2]);
  not not_17 (A[3], out_14[3]);
  not not_18 (A[4], out_14[4]);
  not not_19 (A[5], out_14[5]);
  not not_20 (A[6], out_14[6]);
  not not_21 (A[7], out_14[7]);
  BarrelShifter #(.Bits(8), .barrelShifterMode("rotate")) barrelshifter_3 (
    .in(out_14), .shift(out_15[3:0]), .out(A_lt__lt__lt_B));
  BarrelShifter #(.Bits(8), .barrelShifterMode("rotate"), .direction("right")) barrelshifter_4 (
    .in(out_14), .shift(out_15[3:0]), .out(A_gt__gt__gt_B));

  assign out_19[7:4] = 4'b0000;
  assign out_36 = out_35;

  // Other names for the same wires on the sheet: rRAM_address[3:0] = out_19[3:0]; operand[7:0] = out_47;
  //   operand_3_0[3:0] = out_47[3:0]; operand_7_4[3:0] = out_47[7:4]; opcode[5:0] = out_48;
  //   sel_ALU_ops[3:0] = out_48[3:0]; LCM_1[7:0] = out_42; LCM_2[7:0] = out_43; pRAM_max_index[7:0] = out_35;
  //   pRAM_operand[7:0] = out_35; A_B_t[7:0] = out_23; A_B_t_t[7:0] = out_22; A_plus_B[7:0] = out_21;
  //   a_t[7:0] = out_40; accA[7:0] = out_14; accB[7:0] = out_15; address[7:0] = out_13; ALU[7:0] = out_20;
  //   b[7:0] = out_41; fact[15:0] = out_46; fact_current_state[1:0] = {fact_1_state, fact_0_state};
  //   instruction[13:0] = out_12; LCMa[7:0] = out_38; LCMb[7:0] = out_39; T5 = load_C; T1 = load_instruction;
  //   max[7:0] = out_34; max_current_state[1:0] = {max_1_state, max_0_state}; max_index[7:0] = out_33;
  //   n_t[7:0] = out_45; pRAM_address[7:0] = out_24; regC[7:0] = out_16; regD[7:0] = out_17;
  //   rRAM_operand[7:0] = out_18; sel__eq[1:0] = out_29; sel_A[2:0] = out_25; sel_B[1:0] = out_26;
  //   sel_C[1:0] = out_27; sel_D[1:0] = out_28; sel_rRAM[1:0] = out_30; sel_rRAM_address[2:0] = out_31; op15 = out_32;
  //   selector_pRAM_address = out_32; state_current[4:0] = out_37; T31 = done

  // Notes on the sheet:
  //   state
  //   Decoder
  //   00000 start
  //   00001 fetch
  //   00010 decode
  //   00011 writeA
  //   00100 writeB
  //   00101 writeC
  //   00110 writeD
  //   00111 rRAM[operand]
  //   01000 ALU
  //   01001 CMP
  //   01010 isPrime
  //   01011 reminder
  //   01100 load rRAM[7:4]
  //   01101 writeB
  //   01110 writeD
  //   01111 writeA
  //   10000 write flag
  //   10001 write EQ
  //   10010 write EQ
  //   10011 load rRAM[3:0]
  //   10100 calc LCM
  //   10101 write rRAM
  //   10110 write rRAM
  //   10111 jmp
  //   11000 reset
  //   11001 factorial
  //   11010 max
  //   11011 -
  //   11100 -
  //   11101 halt
  //   11110 result
  //   11111 done
  //   Register
  //   Flag
  //   contents of prime_list (hex, n*v repeats v):
  //   0,0,1,1,0,1,0,1,0,0,0,1,0,1,0,0,0,1,0,1,0,0,0,b,5*0,1,0,1,5*0
  //   ,1,0,0,0,1,0,1,0,0,0,1,5*0,1,5*0,1,0,1,5*0,1,0,0,0,1,0,1,5*0,1
  //   ,0,0,0,1,5*0,1,7*0,1,0,0,0,1,0,1,0,0,0,1,0,1,0,0,0,1,13*0,1,0,0,0
  //   ,1,5*0,1,0,1,9*0,1,0,1,5*0,1,5*0,1,0,0,0,1,5*0,1,5*0,1,0,1,9*0
  //   ,1,0,1,0,0,0,1,0,1,23*0,1,0,0,0,1,5*0,1,5*0,1,0,1,9*0,1
  //   contro-unit
  //   rRAM
  //   contents of rom_1 (hex, n*v repeats v):
  //   0,0,0,1,0,0,2,0,3,5*0,2,4,5,15*0,6*6,0,0,8*6
  //   contents of rom_2 (hex, n*v repeats v):
  //   4*0,1,9*0,2
  //   contents of rom_3 (hex, n*v repeats v):
  //   9*0,1,2,0,0,1
  //   contents of rom_4 (hex, n*v repeats v):
  //   11*0,1,2,2
  //   contents of rom_5 (hex, n*v repeats v):
  //   49*0,1,2
  //   contents of rom_6 (hex, n*v repeats v):
  //   12*0,1,1,5*0,2,0,2,1,0,3,24*0,1,2
  //   contents of rom_7 (hex, n*v repeats v):
  //   12*0,5,6*0,4,0,1,2,0,3,6,6,0,0,0,3,18*0,1,2
  //   Input
  //   pRAM
  //   output
  //   About
  //   Narinthon Yangngam
  //    CEDT Final Project
  //   \n2568
  //    _____Digital Logic
  //    ______Mini CPU
  //   max
  //   Fact
  //   nextstate-condition
  //   contents of nextstate_decode (hex, n*v repeats v):
  //   1,3,4,3,4,5,3,6,3,5,5,6,6,5,3,3,3,7,6*17,8*0,6*8,0,0,8*8,9,a,b
  //   ,c,19,1a,9*0,1d
  //   PC
  //   jump-condition
  //   LCM
  //   ALU
  //   rRAM-counter
  //   Instruction
  //   contents of rom_8 (hex, n*v repeats v):
  //   1,7*0,9*1,2,4,8,10,20,40,80,1,3,9,1b,51,f3,d9,8b,1,4,10,40,100
  //   ,0,0,0,1,5,19,7d,71,35,9,2d,1,6,24,d8,10,60,40,80,1,7,31,57,61
  //   ,b7,71,f7
endmodule

/* Test case 01_P01T01:
M N progIn reset progLoad start result clk valid done output
0 0      0     0        0     0      0   0     x    x      x
0 0      0     0        0     0      0   1     x    x      x
0 0      0     1        0     0      0   0     x    x      x
0 0      0     1        0     0      0   1     0    0      x
0 0      0     0        0     0      0   0     0    0      x
0 0      0     0        0     0      0   1     0    0      x
0 0      0     0        0     0      0   0     0    0      x
0 0      0     0        0     0      0   1     0    0      x
0 0      0     0        0     0      0   0     0    0      x
0 0      0     0        0     0      0   1     0    0      x
0 0      0     0        0     0      0   0     0    0      x
0 0      0     0        0     0      0   1     0    0      x
0 0      0     0        0     0      0   0     0    0      x
0 0      0     0        0     0      0   1     0    0      x
0 0      0     0        0     0      0   0     0    0      x
0 0      0     0        0     0      0   1     0    0      x
0 0      0     0        0     0      0   0     0    0      x
0 0      0     0        0     0      0   1     0    0      x
0 0      0     0        0     0      0   0     0    0      x
0 0      0     0        0     0      0   1     0    0      x
0 0      0     0        0     0      0   0     0    0      x
0 0      0     0        0     0      0   1     0    0      x
0 0      0     0        0     0      0   0     0    0      x
0 0      0     0        0     0      0   1     0    0      x
0 0      0     0        0     0      0   0     0    0      x
0 0      0     0        0     0      0   1     0    0      x
0 0      0     0        0     0      0   0     0    0      x
0 0      0     0        0     0      0   1     0    0      x
0 0      0     0        0     0      0   0     0    0      x
0 0      0     0        0     0      0   1     0    0      x
0 0      0     0        0     0      0   0     0    0      x
0 0      0     0        0     0      0   1     0    0      x
0 0      0     0        0     0      0   0     0    0      x
0 0      0     0        0     0      0   1     0    0      x
0 0      0     0        0     0      0   0     0    0      x
0 0      0     0        0     0      0   1     0    0      x
0 0      0     0        0     0      0   0     0    0      x
0 0      0     0        0     0      0   1     0    0      x
0 0      0     0        0     0      0   0     0    0      x
0 0      0     0        0     0      0   1     0    0      x
0 0      0     0        0     0      0   0     0    0      x
0 0      0     0        0     0      0   1     0    0      x
0 0    271     0        1     0      0   0     0    0      x
0 0    271     0        1     0      0   1     0    0      x
0 0    565     0        1     0      0   0     0    0      x
0 0    565     0        1     0      0   1     0    0      x
0 0   8192     0        1     0      0   0     0    0      x
0 0   8192     0        1     0      0   1     0    0      x
0 0   4355     0        1     0      0   0     0    0      x
0 0   4355     0        1     0      0   1     0    0      x
0 0  16128     0        1     0      0   0     0    0      x
0 0  16128     0        1     0      0   1     0    0      x
0 0      0     0        0     1      0   0     0    0      x
0 0      0     0        0     1      0   1     0    0      x
0 0      0     0        0     0      0   0     x    0      x
0 0      0     0        0     0      0   1     x    0      x
0 0      0     0        0     0      0   0     x    0      x
0 0      0     0        0     0      0   1     x    0      x
0 0      0     0        0     0      0   0     x    0      x
0 0      0     0        0     0      0   1     x    0      x
0 0      0     0        0     0      0   0     x    0      x
0 0      0     0        0     0      0   1     x    0      x
0 0      0     0        0     0      0   0     x    0      x
0 0      0     0        0     0      0   1     x    0      x
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*/

/* Test case 09_P06T02:
M N progIn reset progLoad start result clk valid done output
0 0      0     0        0     0      0   0     x    x      x
0 0      0     0        0     0      0   1     x    x      x
0 0      0     1        0     0      0   0     x    x      x
0 0      0     1        0     0      0   1     0    0      x
0 0      0     0        0     0      0   0     0    0      x
0 0      0     0        0     0      0   1     0    0      x
0 0      0     0        0     0      0   0     0    0      x
0 0      0     0        0     0      0   1     0    0      x
0 0      0     0        0     0      0   0     0    0      x
0 0      0     0        0     0      0   1     0    0      x
0 0      0     0        0     0      0   0     0    0      x
0 0      0     0        0     0      0   1     0    0      x
0 0      0     0        0     0      0   0     0    0      x
0 0      0     0        0     0      0   1     0    0      x
0 0      0     0        0     0      0   0     0    0      x
0 0      0     0        0     0      0   1     0    0      x
0 0      0     0        0     0      0   0     0    0      x
0 0      0     0        0     0      0   1     0    0      x
0 0      0     0        0     0      0   0     0    0      x
0 0      0     0        0     0      0   1     0    0      x
0 0      0     0        0     0      0   0     0    0      x
0 0      0     0        0     0      0   1     0    0      x
0 0      0     0        0     0      0   0     0    0      x
0 0      0     0        0     0      0   1     0    0      x
0 0      0     0        0     0      0   0     0    0      x
0 0      0     0        0     0      0   1     0    0      x
0 0      0     0        0     0      0   0     0    0      x
0 0      0     0        0     0      0   1     0    0      x
0 0      0     0        0     0      0   0     0    0      x
0 0      0     0        0     0      0   1     0    0      x
0 0      0     0        0     0      0   0     0    0      x
0 0      0     0        0     0      0   1     0    0      x
0 0      0     0        0     0      0   0     0    0      x
0 0      0     0        0     0      0   1     0    0      x
0 0      0     0        0     0      0   0     0    0      x
0 0      0     0        0     0      0   1     0    0      x
0 0      0     0        0     0      0   0     0    0      x
0 0      0     0        0     0      0   1     0    0      x
0 0      0     0        0     0      0   0     0    0      x
0 0      0     0        0     0      0   1     0    0      x
0 0      0     0        0     0      0   0     0    0      x
0 0      0     0        0     0      0   1     0    0      x
0 0      0     0        0     0      0   0     0    0      x
0 0      0     0        0     0      0   1     0    0      x
0 0   2304     0        1     0      0   0     0    0      x
0 0   2304     0        1     0      0   1     0    0      x
0 0   1536     0        1     0      0   0     0    0      x
0 0   1536     0        1     0      0   1     0    0      x
0 0   4353     0        1     0      0   0     0    0      x
0 0   4353     0        1     0      0   1     0    0      x
0 0   2560     0        1     0      0   0     0    0      x
0 0   2560     0        1     0      0   1     0    0      x
0 0   1536     0        1     0      0   0     0    0      x
0 0   1536     0        1     0      0   1     0    0      x
0 0   4354     0        1     0      0   0     0    0      x
0 0   4354     0        1     0      0   1     0    0      x
0 0   1024     0        1     0      0   0     0    0      x
0 0   1024     0        1     0      0   1     0    0      x
0 0   4097     0        1     0      0   0     0    0      x
0 0   4097     0        1     0      0   1     0    0      x
0 0   8704     0        1     0      0   0     0    0      x
0 0   8704     0        1     0      0   1     0    0      x
0 0   4355     0        1     0      0   0     0    0      x
0 0   4355     0        1     0      0   1     0    0      x
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*/

/* Test case 17_P02T02:
M N progIn reset progLoad start result clk valid done output
0 0      0     0        0     0      0   0     x    x      x
0 0      0     0        0     0      0   1     x    x      x
0 0      0     1        0     0      0   0     x    x      x
0 0      0     1        0     0      0   1     0    0      x
0 0      0     0        0     0      0   0     0    0      x
0 0      0     0        0     0      0   1     0    0      x
0 0      0     0        0     0      0   0     0    0      x
0 0      0     0        0     0      0   1     0    0      x
0 0      0     0        0     0      0   0     0    0      x
0 0      0     0        0     0      0   1     0    0      x
0 0      0     0        0     0      0   0     0    0      x
0 0      0     0        0     0      0   1     0    0      x
0 0      0     0        0     0      0   0     0    0      x
0 0      0     0        0     0      0   1     0    0      x
0 0      0     0        0     0      0   0     0    0      x
0 0      0     0        0     0      0   1     0    0      x
0 0      0     0        0     0      0   0     0    0      x
0 0      0     0        0     0      0   1     0    0      x
0 0      0     0        0     0      0   0     0    0      x
0 0      0     0        0     0      0   1     0    0      x
0 0      0     0        0     0      0   0     0    0      x
0 0      0     0        0     0      0   1     0    0      x
0 0      0     0        0     0      0   0     0    0      x
0 0      0     0        0     0      0   1     0    0      x
0 0      0     0        0     0      0   0     0    0      x
0 0      0     0        0     0      0   1     0    0      x
0 0      0     0        0     0      0   0     0    0      x
0 0      0     0        0     0      0   1     0    0      x
0 0      0     0        0     0      0   0     0    0      x
0 0      0     0        0     0      0   1     0    0      x
0 0      0     0        0     0      0   0     0    0      x
0 0      0     0        0     0      0   1     0    0      x
0 0      0     0        0     0      0   0     0    0      x
0 0      0     0        0     0      0   1     0    0      x
0 0      0     0        0     0      0   0     0    0      x
0 0      0     0        0     0      0   1     0    0      x
0 0      0     0        0     0      0   0     0    0      x
0 0      0     0        0     0      0   1     0    0      x
0 0      0     0        0     0      0   0     0    0      x
0 0      0     0        0     0      0   1     0    0      x
0 0      0     0        0     0      0   0     0    0      x
0 0      0     0        0     0      0   1     0    0      x
0 0    510     0        1     0      0   0     0    0      x
0 0    510     0        1     0      0   1     0    0      x
0 0    514     0        1     0      0   0     0    0      x
0 0    514     0        1     0      0   1     0    0      x
0 0  12288     0        1     0      0   0     0    0      x
0 0  12288     0        1     0      0   1     0    0      x
0 0   4869     0        1     0      0   0     0    0      x
0 0   4869     0        1     0      0   1     0    0      x
0 0   4353     0        1     0      0   0     0    0      x
0 0   4353     0        1     0      0   1     0    0      x
0 0   5127     0        1     0      0   0     0    0      x
0 0   5127     0        1     0      0   1     0    0      x
0 0   4354     0        1     0      0   0     0    0      x
0 0   4354     0        1     0      0   1     0    0      x
0 0   5385     0        1     0      0   0     0    0      x
0 0   5385     0        1     0      0   1     0    0      x
0 0   4355     0        1     0      0   0     0    0      x
0 0   4355     0        1     0      0   1     0    0      x
0 0   5643     0        1     0      0   0     0    0      x
0 0   5643     0        1     0      0   1     0    0      x
0 0   4356     0        1     0      0   0     0    0      x
0 0   4356     0        1     0      0   1     0    0      x
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*/

/* Test case 25_P09T03:
M N progIn reset progLoad start result clk valid done output
0 0      0     0        0     0      0   0     x    x      x
0 0      0     0        0     0      0   1     x    x      x
0 0      0     1        0     0      0   0     x    x      x
0 0      0     1        0     0      0   1     0    0      x
0 0      0     0        0     0      0   0     0    0      x
0 0      0     0        0     0      0   1     0    0      x
0 0      0     0        0     0      0   0     0    0      x
0 0      0     0        0     0      0   1     0    0      x
0 0      0     0        0     0      0   0     0    0      x
0 0      0     0        0     0      0   1     0    0      x
0 0      0     0        0     0      0   0     0    0      x
0 0      0     0        0     0      0   1     0    0      x
0 0      0     0        0     0      0   0     0    0      x
0 0      0     0        0     0      0   1     0    0      x
0 0      0     0        0     0      0   0     0    0      x
0 0      0     0        0     0      0   1     0    0      x
0 0      0     0        0     0      0   0     0    0      x
0 0      0     0        0     0      0   1     0    0      x
0 0      0     0        0     0      0   0     0    0      x
0 0      0     0        0     0      0   1     0    0      x
0 0      0     0        0     0      0   0     0    0      x
0 0      0     0        0     0      0   1     0    0      x
0 0      0     0        0     0      0   0     0    0      x
0 0      0     0        0     0      0   1     0    0      x
0 0      0     0        0     0      0   0     0    0      x
0 0      0     0        0     0      0   1     0    0      x
0 0      0     0        0     0      0   0     0    0      x
0 0      0     0        0     0      0   1     0    0      x
0 0      0     0        0     0      0   0     0    0      x
0 0      0     0        0     0      0   1     0    0      x
0 0      0     0        0     0      0   0     0    0      x
0 0      0     0        0     0      0   1     0    0      x
0 0      0     0        0     0      0   0     0    0      x
0 0      0     0        0     0      0   1     0    0      x
0 0      0     0        0     0      0   0     0    0      x
0 0      0     0        0     0      0   1     0    0      x
0 0      0     0        0     0      0   0     0    0      x
0 0      0     0        0     0      0   1     0    0      x
0 0      0     0        0     0      0   0     0    0      x
0 0      0     0        0     0      0   1     0    0      x
0 0      0     0        0     0      0   0     0    0      x
0 0      0     0        0     0      0   1     0    0      x
0 0      0     0        0     0      0   0     0    0      x
0 0      0     0        0     0      0   1     0    0      x
0 0   2304     0        1     0      0   0     0    0      x
0 0   2304     0        1     0      0   1     0    0      x
0 0   1536     0        1     0      0   0     0    0      x
0 0   1536     0        1     0      0   1     0    0      x
0 0   4352     0        1     0      0   0     0    0      x
0 0   4352     0        1     0      0   1     0    0      x
0 0   2560     0        1     0      0   0     0    0      x
0 0   2560     0        1     0      0   1     0    0      x
0 0   1536     0        1     0      0   0     0    0      x
0 0   1536     0        1     0      0   1     0    0      x
0 0   4353     0        1     0      0   0     0    0      x
0 0   4353     0        1     0      0   1     0    0      x
0 0   1024     0        1     0      0   0     0    0      x
0 0   1024     0        1     0      0   1     0    0      x
0 0   4096     0        1     0      0   0     0    0      x
0 0   4096     0        1     0      0   1     0    0      x
0 0  10240     0        1     0      0   0     0    0      x
0 0  10240     0        1     0      0   1     0    0      x
0 0   4354     0        1     0      0   0     0    0      x
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*/

/* Test case 02_P01T02:
M N progIn reset progLoad start result clk valid done output
0 0      0     0        0     0      0   0     x    x      x
0 0      0     0        0     0      0   1     x    x      x
0 0      0     1        0     0      0   0     x    x      x
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*/

/* Test case 10_P07T01:
M N progIn reset progLoad start result clk valid done output
0 0      0     0        0     0      0   0     x    x      x
0 0      0     0        0     0      0   1     x    x      x
0 0      0     1        0     0      0   0     x    x      x
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*/

/* Test case 18_P03T03:
M N progIn reset progLoad start result clk valid done output
0 0      0     0        0     0      0   0     x    x      x
0 0      0     0        0     0      0   1     x    x      x
0 0      0     1        0     0      0   0     x    x      x
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*/

/* Test case 26_P10T2:
M N progIn reset progLoad start result clk valid done output
0 0      0     0        0     0      0   0     x    x      x
0 0      0     0        0     0      0   1     x    x      x
0 0      0     1        0     0      0   0     x    x      x
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*/

/* Test case 03_P02T01:
M N progIn reset progLoad start result clk valid done output
0 0      0     0        0     0      0   0     x    x      x
0 0      0     0        0     0      0   1     x    x      x
0 0      0     1        0     0      0   0     x    x      x
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*/

/* Test case 11_P07T02:
M N progIn reset progLoad start result clk valid done output
0 0      0     0        0     0      0   0     x    x      x
0 0      0     0        0     0      0   1     x    x      x
0 0      0     1        0     0      0   0     x    x      x
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*/

/* Test case 19_P04T02:
M N progIn reset progLoad start result clk valid done output
0 0      0     0        0     0      0   0     x    x      x
0 0      0     0        0     0      0   1     x    x      x
0 0      0     1        0     0      0   0     x    x      x
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*/

/* Test case 27_P10T02:
M N progIn reset progLoad start result clk valid done output
0 0      0     0        0     0      0   0     x    x      x
0 0      0     0        0     0      0   1     x    x      x
0 0      0     1        0     0      0   0     x    x      x
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*/

/* Test case 04_P03T01:
M N progIn reset progLoad start result clk valid done output
0 0      0     0        0     0      0   0     x    x      x
0 0      0     0        0     0      0   1     x    x      x
0 0      0     1        0     0      0   0     x    x      x
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*/

/* Test case 12_P08T01:
M N progIn reset progLoad start result clk valid done output
0 0      0     0        0     0      0   0     x    x      x
0 0      0     0        0     0      0   1     x    x      x
0 0      0     1        0     0      0   0     x    x      x
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*/

/* Test case 20_P04T4:
M N progIn reset progLoad start result clk valid done output
0 0      0     0        0     0      0   0     x    x      x
0 0      0     0        0     0      0   1     x    x      x
0 0      0     1        0     0      0   0     x    x      x
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*/

/* Test case 28_P11T2:
M N progIn reset progLoad start result clk valid done output
0 0      0     0        0     0      0   0     x    x      x
0 0      0     0        0     0      0   1     x    x      x
0 0      0     1        0     0      0   0     x    x      x
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*/

/* Test case 05_P03T02:
M N progIn reset progLoad start result clk valid done output
0 0      0     0        0     0      0   0     x    x      x
0 0      0     0        0     0      0   1     x    x      x
0 0      0     1        0     0      0   0     x    x      x
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*/

/* Test case 13_P08T02:
M N progIn reset progLoad start result clk valid done output
0 0      0     0        0     0      0   0     x    x      x
0 0      0     0        0     0      0   1     x    x      x
0 0      0     1        0     0      0   0     x    x      x
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*/

/* Test case 21_P05T2:
M N progIn reset progLoad start result clk valid done output
0 0      0     0        0     0      0   0     x    x      x
0 0      0     0        0     0      0   1     x    x      x
0 0      0     1        0     0      0   0     x    x      x
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*/

/* Test case 29_P11T02:
M N progIn reset progLoad start result clk valid done output
0 0      0     0        0     0      0   0     x    x      x
0 0      0     0        0     0      0   1     x    x      x
0 0      0     1        0     0      0   0     x    x      x
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*/

/* Test case 06_P04T01:
M N progIn reset progLoad start result clk valid done output
0 0      0     0        0     0      0   0     x    x      x
0 0      0     0        0     0      0   1     x    x      x
0 0      0     1        0     0      0   0     x    x      x
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*/

/* Test case 14_P09T01:
M N progIn reset progLoad start result clk valid done output
0 0      0     0        0     0      0   0     x    x      x
0 0      0     0        0     0      0   1     x    x      x
0 0      0     1        0     0      0   0     x    x      x
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*/

/* Test case 22_P06T03:
M N progIn reset progLoad start result clk valid done output
0 0      0     0        0     0      0   0     x    x      x
0 0      0     0        0     0      0   1     x    x      x
0 0      0     1        0     0      0   0     x    x      x
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*/

/* Test case 07_P05T01:
M N progIn reset progLoad start result clk valid done output
0 0      0     0        0     0      0   0     x    x      x
0 0      0     0        0     0      0   1     x    x      x
0 0      0     1        0     0      0   0     x    x      x
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*/

/* Test case 15_P09T02:
M N progIn reset progLoad start result clk valid done output
0 0      0     0        0     0      0   0     x    x      x
0 0      0     0        0     0      0   1     x    x      x
0 0      0     1        0     0      0   0     x    x      x
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*/

/* Test case 23_P07T03:
M N progIn reset progLoad start result clk valid done output
0 0      0     0        0     0      0   0     x    x      x
0 0      0     0        0     0      0   1     x    x      x
0 0      0     1        0     0      0   0     x    x      x
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*/

/* Test case 08_P06T01:
M N progIn reset progLoad start result clk valid done output
0 0      0     0        0     0      0   0     x    x      x
0 0      0     0        0     0      0   1     x    x      x
0 0      0     1        0     0      0   0     x    x      x
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*/

/* Test case 16_P01T03:
M N progIn reset progLoad start result clk valid done output
0 0      0     0        0     0      0   0     x    x      x
0 0      0     0        0     0      0   1     x    x      x
0 0      0     1        0     0      0   0     x    x      x
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*/

/* Test case 24_P08T03:
M N progIn reset progLoad start result clk valid done output
0 0      0     0        0     0      0   0     x    x      x
0 0      0     0        0     0      0   1     x    x      x
0 0      0     1        0     0      0   0     x    x      x
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*/
